# Fritzing sketch Massa Jenis (saved by Fritzing 0.9.3b)
breadboards: 1

parts:
  Part1 = Arduino Uno (Rev3)
  Keypad4x1 = Keypad Membran 4x4
  Part2 = LCD1602-I2C
  Load_Cell1 = Load Cell - Red/white/black/green
  Part3 = HX711 Weighing Sensor Module
  HC-SR04_Sensor_1 = HC-SR04 Ultrasonic Distance Sensor

nets:
  N1: Part1.D8, Keypad4x1.Pin2
  N2: Part1.D9_PWM, Keypad4x1.Pin1
  N3: Part1.D10_PWM/SS, HC-SR04_Sensor_1.TRIG
  N4: Part1.D11_PWM/MOSI, HC-SR04_Sensor_1.ECHO
  N5: Part1.D12/MISO, Part3.CK/TX
  N6: Part1.D13/SCK, Part3.DO/RX
  N7: Part1.A4/SDA, Part2.SDA
  N8: Part1.A5/SCL, Part2.SCL
  N9: Part1.D2, Keypad4x1.Pin8
  N10: Part1.D3_PWM, Keypad4x1.Pin7
  N11: Part1.D4, Keypad4x1.Pin6
  N12: Part1.D5_PWM, Keypad4x1.Pin5
  N13: Part1.D6_PWM, Keypad4x1.Pin4
  N14: Part1.D7, Keypad4x1.Pin3
  VCC: Part1.5V, Part2.VCC, Part3.VCC, HC-SR04_Sensor_1.VCC
  GND: Part1.GND, Part2.GND, Part3.GND, HC-SR04_Sensor_1.GND
  N15: Load_Cell1.wire1, Part3.E+
  N16: Load_Cell1.wire2, Part3.A-
  N17: Load_Cell1.wire3, Part3.E-
  N18: Load_Cell1.wire4, Part3.A+

custom parts:
  Keypad Membran 4x4: Membrane Keypad 4x4 Matrix
  LCD1602-I2C: A standard character display, usually with 2x16 characters. Comes in many colors with LCM1602 IIC attached.
  Load Cell - Red/white/black/green: A rectangle load cell/weighting pressure Sensor with four wires - Red, white, black, green. Normally corresponding with E+, E-, A+, A- respectively.
  HX711 Weighing Sensor Module: HX711 is a precision 24-bit analog-to-digital converter (ADC) designed for weigh scales and industrial control applications to interface directly with a bridge sensor.
